// Logisim project Lab 1.circ as structural Verilog: 4 circuits, main circuit 2:1 Multiplexer
module _2_1_Multiplexer (
  input  A,
  input  B,
  input  Selector,
  output Output
);

  wire and_1_out, and_2_out, not_1_out;

  not not_1 (not_1_out, Selector);
  and and_1 (and_1_out, A, A, not_1_out);
  and and_2 (and_2_out, Selector, B);
  or or_1 (Output, and_1_out, and_2_out);
endmodule

module _2_1_Multiplex_NAND_only (
  input  A,
  input  Selector,
  input  B,
  output Output
);

  wire nand_1_out, nand_2_out, nand_3_out;

  not nand_1 (nand_1_out, Selector);  // NAND_Gate
  nand nand_2 (nand_2_out, A, nand_1_out);
  nand nand_3 (nand_3_out, Selector, B);
  nand nand_4 (Output, nand_2_out, nand_3_out);
endmodule

module _4_1_Mux (
  input  A,
  input  B,
  input  C,
  input  D,
  input  S0,
  input  S1,
  output out_7
);

  wire n2_1_multiplexer_1_output, n2_1_multiplexer_2_output;

  _2_1_Multiplexer u_2_1_multiplexer_1 (.A(A), .B(B), .Selector(S1), .Output(n2_1_multiplexer_1_output));
  _2_1_Multiplexer u_2_1_multiplexer_2 (.A(C), .B(D), .Output(n2_1_multiplexer_2_output));  // open: Selector
  _2_1_Multiplexer u_2_1_multiplexer_3 (
    .A(n2_1_multiplexer_1_output), .B(n2_1_multiplexer_2_output), .Selector(S0), .Output(out_7));
endmodule

module _8_1_Mux (
  input  _00,
  input  _01,
  input  _02,
  input  _03,
  input  S0,
  input  S1,
  input  S2,
  input  _10,
  input  _11,
  input  _12,
  input  _13,
  output out_12
);

  wire n4_1_mux_1_out_7, n4_1_mux_2_out_7;

  _4_1_Mux u_4_1_mux_1 (.A(_10), .B(_11), .C(_12), .D(_13), .S0(S0), .S1(S1), .out_7(n4_1_mux_1_out_7));
  _4_1_Mux u_4_1_mux_2 (.A(_00), .B(_01), .C(_02), .D(_03), .S0(S0), .S1(S1), .out_7(n4_1_mux_2_out_7));
  _2_1_Multiplexer u_2_1_multiplexer_1 (.A(n4_1_mux_2_out_7), .B(n4_1_mux_1_out_7), .Selector(S2), .Output(out_12));
endmodule
